# Fritzing sketch adns5050_arduino (saved by Fritzing 0.6.2b)
breadboards: 1

parts:
  Arduino1 = Arduino
  C1 = Tantalum Capacitor [capacitance=3.3mF rated_voltage=35V package="100 mil [THT, tantalum]"]
  C4 = Ceramic Capacitor [capacitance=4.7mF rated_voltage=35V package="100 mil [THT, multilayer]"]
  U1 = mystery part, 8 pins [chip_label=? spacing=300mil]
  C5 = Ceramic Capacitor [capacitance=100nF package="100 mil [THT, multilayer]"]
  C2 = Tantalum Capacitor [capacitance=100nF package="100 mil [THT, tantalum]"]

nets:
  N1: Arduino1.GND, C1.-, C4.1, U1.pin6, C5.1, C2.-
  N2: Arduino1.D4, U1.pin4
  N3: Arduino1.D3, U1.pin3
  N4: Arduino1.+5V, C4.0, U1.pin5, C2.+
  N5: Arduino1.A4, U1.pin1
  N6: Arduino1.A5, U1.pin8
  N7: C1.+, U1.pin7, C5.0
